# Fritzing sketch Belichtungs-Messer (saved by Fritzing 0.8.3b)
perfboards: 1

parts:
  LED2 = LED - 3mm [color="Green (560nm)" package="3 mm [THT]"]  # not connected
  R1 = Resistor [tolerance=±5% resistance=10k package=THT]  # not connected
  R3 = Resistor [tolerance=±5% resistance=470 package=THT]  # not connected
  S2 = Pushbutton [package="[THT]"]
  R4 = Resistor [tolerance=±5% resistance=470 package=THT]  # not connected
  LED1 = LED - 3mm [color="Red (633nm)" package="3 mm [THT]"]  # not connected
  S1 = Pushbutton [package="[THT]"]
  R2 = Resistor [tolerance=±5% resistance=10k package=THT]  # not connected
  LDR = Photocell (LDR) [package=THT]  # not connected
  R5 = Resistor [tolerance=±5% resistance=10k package=THT]  # not connected
  J3 = male pin header, 2 pins [form="♂ (male)"]
  J2 = male pin header, 2 pins [form="♂ (male)"]
  J1 = male pin header, 2 pins [form="♂ (male)"]
  J5 = male pin header, 2 pins [form="♂ (male)"]
  J6 = male pin header, 2 pins [form="♂ (male)"]
  J7 = male pin header, 2 pins [form="♂ (male)"]
  J8 = male pin header, 2 pins [form="♂ (male)"]
  J9 = male pin header, 2 pins [form="♂ (male)"]
  R6 = Rotary Potentiometer (Small)  # not connected
  J4 = male pin header, 2 pins [form="♂ (male)"]
  Bauteil1 = Arduino Uno (Rev3)

nets:
  N1: S2.Pin_1, S2.Pin_2
  N2: S2.Pin_3, S2.Pin_4
  N3: S1.Pin_1, S1.Pin_2
  N4: S1.Pin_3, S1.Pin_4
  N5: J3.pin1, J3.pin2
  N6: J2.pin1, Bauteil1.ICSP_MOSI, Bauteil1.D11_PWM/MOSI
  N7: J1.pin1, Bauteil1.D10_PWM/SS
  N8: J5.pin2, Bauteil1.A0
  N9: J6.pin2, Bauteil1.A2
  N10: J7.pin1, Bauteil1.5V
  N11: J7.pin2, Bauteil1.GND
  N12: J8.pin1, Bauteil1.D7
  N13: J9.pin1, Bauteil1.D6_PWM
  N14: J4.pin1, J4.pin2

notes:
  GND
  VCC
  Btn1
  Btn2
  LED1
  LED2
  LDR
  Poti
