# Fritzing sketch Encoder-Modul (saved by Fritzing 0.9.0b)
circuit board: 4cm x 2cm
breadboards: 1

parts:
  R1 = Resistor [tolerance=±5% resistance=1k package=THT]
  R2 = Resistor [tolerance=±5% resistance=1k package=THT]
  R4 = Resistor [tolerance=±5% resistance=470 package=THT]
  R5 = Resistor [tolerance=±5% resistance=1k package=THT]
  R6 = Resistor [tolerance=±5% resistance=2.2k package=THT]
  R7 = Resistor [tolerance=±5% resistance=4.7k package=THT]
  R8 = Resistor [tolerance=±5% resistance=10k package=THT]
  RE1 = Rotary Encoder (Bourns PEC11-4xxxK-Sxxxx) [package=THT]
  J5 = male pin header, 2 pins [form="♂ (male)"]
  J6 = male pin header, 2 pins [form="♂ (male)"]
  J7 = male pin header, 2 pins [form="♂ (male)"]
  J8 = male pin header, 2 pins [form="♂ (male)"]
  J1 = male pin header, 5 pins [form="♂ (male)"]
  R3 = Resistor [tolerance=±5% resistance=4.7k package=THT]

nets:
  N1: R1.Pin_0, R2.Pin_1, J1.pin2, R3.Pin_0
  N2: R1.Pin_1, RE1.CH-A, J1.pin3
  N3: R2.Pin_0, RE1.CH-B, J1.pin4
  N4: R4.Pin_0, R5.Pin_0, R6.Pin_0, R7.Pin_0, R8.Pin_0, J1.pin5, R3.Pin_1
  N5: R4.Pin_1, RE1.BTN#4
  N6: R5.Pin_1, J5.pin2
  N7: R6.Pin_1, J6.pin2
  N8: R7.Pin_1, J7.pin2
  N9: R8.Pin_1, J8.pin2
  N10: RE1.COMM, RE1.BTN#3, J5.pin1, J6.pin1, J7.pin1, J8.pin1, J1.pin1

notes:
  enc-v1
  GND
  VCC
  D1
  D2
  A
  G
  V
  1
  2
  3

custom parts:
  Rotary Encoder (Bourns PEC11-4xxxK-Sxxxx): Rotary Encoder Bourns PEC11-4xxxK-Sxxxx.
