# Fritzing sketch Foto-Shield-v2 (saved by Fritzing 0.9.0b)
circuit board: 10.1776cm x 5.36194cm
perfboards: 1

parts:
  J1 = male pin header, 5 pins [form="♂ (male)"]
  J2 = male pin header, 5 pins [form="♂ (male)"]
  J3 = male pin header, 5 pins [form="♂ (male)"]
  J5 = male pin header, 5 pins [form="♂ (male)"]
  J4 = male pin header, 5 pins [form="♂ (male)"]
  J6 = male pin header, 5 pins [form="♂ (male)"]
  J7 = male pin header, 5 pins [form="♂ (male)"]
  J8 = male pin header, 5 pins [form="♂ (male)"]
  J15 = male pin header, 3 pins [form="♂ (male)"]
  J16 = male pin header, 3 pins [form="♂ (male)"]
  J11 = male pin header, 3 pins [form="♂ (male)"]
  J9 = male pin header, 3 pins [form="♂ (male)"]
  J10 = male pin header, 3 pins [form="♂ (male)"]
  J12 = male pin header, 3 pins [form="♂ (male)"]
  J13 = male pin header, 3 pins [form="♂ (male)"]
  J14 = male pin header, 3 pins [form="♂ (male)"]
  J17 = male pin header, 3 pins [form="♂ (male)"]
  J18 = male pin header, 3 pins [form="♂ (male)"]
  J19 = male pin header, 4 pins [form="♂ (male)"]
  R2 = Resistor [tolerance=±5% resistance=4.7k package=THT]
  R1 = Resistor [tolerance=±5% resistance=4.7k package=THT]
  C1 = Electrolytic Capacitor [capacitance=0.47mF package="100 mil [THT, electrolytic]"]
  C2 = Electrolytic Capacitor [capacitance=0.47mF package="100 mil [THT, electrolytic]"]
  J21 = male pin header, 3 pins [form="♂ (male)"]
  part = male pin header, 3 pins [form="♂ (male)"]  # not connected
  foto-shield-v2 = Arduino Mega ADK (Rev3)
  J20 = Screw terminal - 2 pins [package=THT]

nets:
  N1: J1.pin1, J2.pin1, J3.pin1, J5.pin1, J4.pin1, J6.pin1, J7.pin1, J8.pin1, J11.pin3, J9.pin3, J10.pin3, J12.pin3, J13.pin3, J14.pin3, J19.pin4, C1.-, C2.-, foto-shield-v2.GND, J20.pin2
  N2: J1.pin2, J2.pin2, J3.pin2, J5.pin2, J4.pin2, J6.pin2, J7.pin2, J11.pin2, J9.pin2, J10.pin2, J12.pin2, J13.pin2, J14.pin2, J19.pin3, R2.Pin_1, R1.Pin_1, C1.+, C2.+, J21.pin1, foto-shield-v2.IOREF, foto-shield-v2.5V
  N3: J1.pin3, foto-shield-v2.D13_PWM
  N4: J1.pin4, foto-shield-v2.D12_PWM
  N5: J1.pin5, J9.pin1, foto-shield-v2.A1
  N6: J2.pin3, foto-shield-v2.D11_PWM
  N7: J2.pin4, foto-shield-v2.D10_PWM
  N8: J2.pin5, J10.pin1, foto-shield-v2.A0
  N9: J3.pin3, foto-shield-v2.D9_PWM
  N10: J3.pin4, foto-shield-v2.D8_PWM
  N11: J3.pin5, J11.pin1, foto-shield-v2.A3
  N12: J5.pin3, foto-shield-v2.D2_PWM
  N13: J5.pin4, foto-shield-v2.D3_PWM
  N14: J5.pin5, J13.pin1, foto-shield-v2.A6
  N15: J4.pin3, foto-shield-v2.D7_PWM
  N16: J4.pin4, foto-shield-v2.D6_PWM
  N17: J4.pin5, J12.pin1, foto-shield-v2.A2
  N18: J6.pin3, foto-shield-v2.D4_PWM
  N19: J6.pin4, foto-shield-v2.D5_PWM
  N20: J6.pin5, J14.pin1, foto-shield-v2.A7
  N21: J7.pin3, J15.pin2, R1.Pin_0
  N22: J7.pin4, J16.pin2, R2.Pin_0
  N23: J7.pin5, foto-shield-v2.A8
  N24: J8.pin2, J21.pin2
  N25: J8.pin3, J17.pin2
  N26: J8.pin4, J18.pin2
  N27: J8.pin5, foto-shield-v2.A9
  N28: J15.pin1, foto-shield-v2.A4
  N29: J15.pin3, foto-shield-v2.D20/SDA
  N30: J16.pin1, foto-shield-v2.A5
  N31: J16.pin3, foto-shield-v2.D21/SCL
  N32: J17.pin3, foto-shield-v2.D19/RX1
  N33: J18.pin3, foto-shield-v2.D18/TX1
  N34: J19.pin1, foto-shield-v2.D14/TX3
  N35: J19.pin2, foto-shield-v2.D15/RX3
  N36: J21.pin3, foto-shield-v2.3V3
  N37: foto-shield-v2.VIN, J20.pin1

notes:
  I2C
  seriell
  D13
  D12
  D11
  D10
  A0
  A1
  A3
  A2
  A7
  A6
  A8
  A9
  VCC
  GND
  SDA
  SCL
  RX
  TX
  D9
  D8
  D7
  D6
  D5
  D4
  D3
  D2
  Uno
  o-o o
  o o-o
  Mega
  VIN
  serial
  5V
  3V3
  foto-shield-v2
