# Fritzing sketch Joystick-Modul (saved by Fritzing 0.9.0b)
circuit board: 4cm x 2cm
breadboards: 1

parts:
  R1 = Resistor [tolerance=±5% resistance=4.7k package=THT]
  R2 = Resistor [tolerance=±5% resistance=470 package=THT]
  R3 = Resistor [tolerance=±5% resistance=1k package=THT]
  R6 = Resistor [tolerance=±5% resistance=10k package=THT]
  R5 = Resistor [tolerance=±5% resistance=4.7k package=THT]
  R4 = Resistor [tolerance=±5% resistance=2.2k package=THT]
  U1 = Alps SKQU Joystick [package=THT]
  R7 = Resistor [tolerance=±5% resistance=22k package=THT]
  R8 = Resistor [tolerance=±5% resistance=47k package=THT]
  J2 = male pin header, 2 pins [form="♂ (male)"]
  J3 = male pin header, 2 pins [form="♂ (male)"]
  J1 = male pin header, 3 pins [form="♂ (male)"]

nets:
  N1: R1.Pin_0, J1.pin2
  N2: R1.Pin_1, R2.Pin_0, R3.Pin_0, R6.Pin_0, R5.Pin_0, R4.Pin_0, R7.Pin_0, R8.Pin_0, J1.pin3
  N3: R2.Pin_1, U1.CENTER
  N4: R3.Pin_1, U1.D
  N5: R6.Pin_1, U1.A
  N6: R5.Pin_1, U1.B
  N7: R4.Pin_1, U1.C
  N8: U1.COMM, J2.pin2, J3.pin2, J1.pin1
  N9: R7.Pin_1, J2.pin1
  N10: R8.Pin_1, J3.pin1

notes:
  joy-v1
  GND
  VCC
  A

custom parts:
  Alps SKQU Joystick: 4 way digital joystick with center button
