# Fritzing sketch Mini-Foto-Controller (saved by Fritzing 0.9.0b)
circuit board: 5.62408cm x 5.10336cm
breadboards: 1

parts:
  U1 = atmega328 [package=dip]
  FTDI = male pin header, 6 pins [form="♂ (male)"]
  RF24 = female pin header, 4 pins [form="♀ (female)"]
  J3 = female pin header, 4 pins [form="♀ (female)"]
  J2 = male pin header, 4 pins [form="♂ (male)"]
  J4 = male pin header, 4 pins [form="♂ (male)"]
  J14 = male pin header, 2 pins [form="♂ (male)"]
  J15 = male pin header, 4 pins [form="♂ (male)"]
  J16 = male pin header, 4 pins [form="♂ (male)"]
  J17 = male pin header, 2 pins [form="♂ (male)"]
  J18 = male pin header, 2 pins [form="♂ (male)"]
  XTAL1 = Crystal [frequency="8 MHz" package=THT]
  C3 = Ceramic Capacitor [capacitance=10pF package="100 mil [THT, multilayer]"]
  C4 = Ceramic Capacitor [capacitance=10pF package="100 mil [THT, multilayer]"]
  C5 = Ceramic Capacitor [capacitance=100nF package="100 mil [THT, multilayer]"]
  R1 = Resistor [tolerance=±5% resistance=10k package=THT]
  R2 = Resistor [tolerance=±5% resistance=4.7k package=THT]
  R3 = Resistor [tolerance=±5% resistance=4.7k package=THT]
  C2 = Ceramic Capacitor [capacitance=100nF package="100 mil [THT, multilayer]"]
  C1 = Ceramic Capacitor [capacitance=100nF package="100 mil [THT, multilayer]"]
  J20 = male pin header, 5 pins [form="♂ (male)"]
  J21 = male pin header, 5 pins [form="♂ (male)"]
  J22 = male pin header, 5 pins [form="♂ (male)"]
  J23 = male pin header, 5 pins [form="♂ (male)"]
  J1 = male pin header, 5 pins [form="♂ (male)"]
  J3_2 = male pin header, 5 pins [form="♂ (male)"]
  ISP = double row male pin header, 6 pins [form="♂ (male)"]
  J11 = male pin header, 4 pins [form="♂ (male)"]
  M4/I2C = male pin header, 5 pins [form="♂ (male)"]
  M1 = male pin header, 5 pins [form="♂ (male)"]
  M3 = male pin header, 5 pins [form="♂ (male)"]
  M2 = male pin header, 5 pins [form="♂ (male)"]
  S1 = Toggle Switch [package=THT]
  J10 = male pin header, 4 pins [form="♂ (male)"]
  Pow = male pin header, 3 pins [form="♂ (male)"]
  J24 = double row female pin header, 26 pins [form="♀ (female)"]
  ext = Screw terminal - 2 pins [package=THT]
  J26 = male pin header, 2 pins [form="♂ (male)"]
  C6 = Electrolytic Capacitor [capacitance=1µF package="100 mil [THT, electrolytic]"]
  J27 = male pin header, 2 pins [form="♂ (male)"]

nets:
  N1: U1.RESET, C5.1, R1.Pin_0, ISP.pin3
  N2: U1.D0_(RX), FTDI.pin4, J1.pin1
  N3: U1.D1_(TX), FTDI.pin5, J1.pin2
  N4: U1.D2, J3.pin4, J1.pin3
  N5: U1.D3_(PWM), J1.pin4, M1.pin3
  N6: U1.D4, J1.pin5, M1.pin4
  N7: U1.VCC, U1.AVCC, J3.pin1, J16.pin1, J16.pin2, J16.pin3, J16.pin4, J18.pin1, J18.pin2, R1.Pin_1, R2.Pin_0, R3.Pin_0, C2.1, C1.0, J21.pin1, J21.pin2, J21.pin3, J21.pin4, J21.pin5, J23.pin1, J23.pin2, J23.pin3, J23.pin4, J23.pin5, ISP.pin4, J11.pin1, J11.pin2, J11.pin3, J11.pin4, M4/I2C.pin2, M1.pin2, M3.pin2, M2.pin2, Pow.pin3, J26.pin1, C6.+, J27.pin2
  N8: U1.GND, FTDI.pin1, RF24.pin1, J15.pin1, J15.pin2, J15.pin3, J15.pin4, J17.pin1, J17.pin2, C3.0, C4.1, C2.0, C1.1, J20.pin1, J20.pin2, J20.pin3, J20.pin4, J20.pin5, J22.pin1, J22.pin2, J22.pin3, J22.pin4, J22.pin5, ISP.pin6, M4/I2C.pin1, M1.pin1, M3.pin1, M2.pin1, J10.pin1, J10.pin2, J10.pin3, J10.pin4, Pow.pin2, J24.pin24, ext.pin1, C6.-
  N9: U1.XLAT1, XTAL1.pin_0, C3.1
  N10: U1.XLAT2, XTAL1.pin_1, C4.0
  N11: U1.D5_(PWM), J2.pin1, M2.pin3
  N12: U1.D6_(PWM), J2.pin2, M2.pin4
  N13: U1.D7, J2.pin3, M3.pin3
  N14: U1.D8, J2.pin4, M3.pin4
  N15: U1.D9_(PWM), RF24.pin2, J3_2.pin5
  N16: U1.D10_(PWM), J3.pin2, J3_2.pin4
  N17: U1.D11_(PWM), J3.pin3, J3_2.pin3, ISP.pin5
  N18: U1.D12, RF24.pin4, J3_2.pin2, ISP.pin1
  N19: U1.D13, RF24.pin3, J3_2.pin1, ISP.pin2
  N20: U1.A0, J4.pin4, M3.pin5
  N21: U1.A1, J4.pin3, M2.pin5
  N22: U1.A2, J4.pin2, M1.pin5
  N23: U1.A3, J4.pin1, M4/I2C.pin5
  N24: U1.A4, J14.pin2, R3.Pin_1, M4/I2C.pin3, J24.pin2
  N25: U1.A5, J14.pin1, R2.Pin_1, M4/I2C.pin4, J24.pin3
  N26: FTDI.pin3, J26.pin2
  N27: FTDI.pin6, C5.0
  N28: S1.L1, ext.pin2
  N29: S1.COM, Pow.pin1
  N30: J24.pin1, J27.pin1

notes:
  A0
  A3
  A2
  A1
  6
  5
  4
  3
  G
  V
  7
  8
  R
  d
  c
  A 5 4 3 2 1 0
  RX
  TX
  2 3 4
  5 6 7 8
  13 12 11 10 9
  1
  T
  MiniFotoCtrl
  v1.4
  Raspberry Pi
  -
  +
