# Fritzing sketch OptoModul (saved by Fritzing 0.9.0b)
circuit board: 4cm x 2cm
breadboards: 1

parts:
  U1 = Optocoupler [package=THT]
  U2 = Optocoupler [package=THT]
  R1 = Resistor [tolerance=±5% resistance=1k package=THT]
  R2 = Resistor [tolerance=±5% resistance=1k package=THT]
  J1 = female pin header, 5 pins [form="♀ (female)"]
  J2 = male pin header, 2 pins [form="♂ (male)"]
  J3 = male pin header, 2 pins [form="♂ (male)"]
  J4 = Resistor [tolerance=±5% resistance=0 package="0603 [SMD]"]
  J5 = Resistor [tolerance=±5% resistance=0 package="0603 [SMD]"]
  TRS5 = Audio Jack (TRS) 3.5mm [package="PG203J [THT]"]

nets:
  N1: U1.Pin_1, R1.Pin_1
  N2: U1.Pin_2, U2.Pin_2, J1.pin5
  N3: U1.Pin_4, J3.pin2, J5.Pin_0, TRS5.Sleeve
  N4: U1.Pin_5, J3.pin1, TRS5.Tip
  N5: U2.Pin_1, R2.Pin_1
  N6: U2.Pin_4, J2.pin2, J5.Pin_1
  N7: U2.Pin_5, J2.pin1, J4.Pin_1
  N8: R1.Pin_0, J1.pin3
  N9: R2.Pin_0, J1.pin2
  N10: J4.Pin_0, TRS5.Ring

notes:
  opto-v1
  GND
  VCC
  D1
  D2
  A1

custom parts:
  Audio Jack (TRS) 3.5mm: Stereo Jack 3.5mm
