# Fritzing sketch RJ11-Modul-v2 (saved by Fritzing 0.9.0b)
circuit board: 4cm x 2cm
breadboards: 1

parts:
  J1 = female pin header, 5 pins [form="♀ (female)"]
  RJ11 = RJ11 Jack [package=rj11-6]
  J3 = male pin header, 2 pins [form="♂ (male)"]
  J2 = male pin header, 4 pins [form="♂ (male)"]
  J4 = male pin header, 3 pins [form="♂ (male)"]
  U1 = mystery part, 8 pins [chip_label=I2C-LV01]
  J5 = male pin header, 2 pins [form="♂ (male)"]

nets:
  N1: J1.pin2, J2.pin1, U1.pin2
  N2: J1.pin3, J2.pin2, U1.pin3
  N3: J1.pin4, J2.pin3, J4.pin3, U1.pin1
  N4: J1.pin5, J2.pin4, U1.pin4, U1.pin5, J5.pin1
  N5: RJ11.1, J3.pin1
  N6: RJ11.2, J3.pin2
  N7: RJ11.3, J4.pin2
  N8: RJ11.4, J5.pin2
  N9: RJ11.5, U1.pin6
  N10: RJ11.6, U1.pin7
  N11: J4.pin1, U1.pin8

notes:
  GND
  VCC
  D1
  D2
  A
  rj11-v2
  S1
  SCL
  S2
  SDA
