# Fritzing sketch FET-Modul-3fach (saved by Fritzing 0.9.0b)
circuit board: 4cm x 4cm
breadboards: 1

parts:
  R1 = Resistor [tolerance=±5% resistance=1k package=THT]
  R2 = Resistor [tolerance=±5% resistance=100k package=THT]
  Q1 = Basic FET N-Channel [package="TO220 [THT]"]
  D1 = Schottky Diode [part_number=SB540 package="300 mil [THT]"]
  J1 = Screw terminal - 2 pins [package=THT]
  J2 = male pin header, 5 pins [form="♂ (male)"]
  Q2 = Basic FET N-Channel [package="TO220 [THT]"]
  Q3 = Basic FET N-Channel [package="TO220 [THT]"]
  D2 = Schottky Diode [part_number=SB540 package="300 mil [THT]"]
  D3 = Schottky Diode [part_number=SB540 package="300 mil [THT]"]
  R3 = Resistor [tolerance=±5% resistance=100k package=THT]
  R4 = Resistor [tolerance=±5% resistance=100k package=THT]
  J3 = Screw terminal - 2 pins [package=THT]
  J4 = Screw terminal - 2 pins [package=THT]
  R5 = Resistor [tolerance=±5% resistance=1k package=THT]
  R6 = Resistor [tolerance=±5% resistance=1k package=THT]
  J5 = male pin header, 2 pins [form="♂ (male)"]

nets:
  N1: R1.Pin_0, J2.pin3
  N2: R1.Pin_1, R2.Pin_0, Q1.gate
  N3: R2.Pin_1, Q1.drain, J2.pin5, Q2.drain, Q3.drain, R3.Pin_1, R4.Pin_1, J5.pin1
  N4: Q1.source, D1.anode, J1.pin1
  N5: D1.cathode, J1.pin2, D2.cathode, D3.cathode, J3.pin2, J4.pin2, J5.pin2
  N6: J2.pin1, R6.Pin_0
  N7: J2.pin2, R5.Pin_0
  N8: Q2.gate, R3.Pin_0, R5.Pin_1
  N9: Q2.source, D2.anode, J3.pin1
  N10: Q3.gate, R4.Pin_0, R6.Pin_1
  N11: Q3.source, D3.anode, J4.pin1

notes:
  VCC
  GND
  IN
  OUT
  fet-v1
