# Fritzing sketch FET-Modul-v2 (saved by Fritzing 0.9.1b)
circuit board: 4cm x 2cm
breadboards: 1

parts:
  R1 = Resistor [tolerance=±5% resistance=1k package=THT]
  R2 = Resistor [tolerance=±5% resistance=100k package=THT]
  Q1 = Basic FET N-Channel [package="TO220 [THT]"]
  D1 = Schottky Diode [part_number=SB540 package="300 mil [THT]"]
  J1 = screw terminal, 3 pins
  J2 = male pin header, 2 pins [form="♂ (male)"]
  J3 = male pin header, 2 pins [form="♂ (male)"]
  J4 = male pin header, 2 pins [form="♂ (male)"]

nets:
  N1: R1.Pin_0, J2.pin1
  N2: R1.Pin_1, R2.Pin_0, Q1.gate
  N3: R2.Pin_1, Q1.source, J1.pin3, J2.pin2, J3.pin1, J4.pin1
  N4: Q1.drain, D1.anode, J1.pin2
  N5: D1.cathode, J1.pin1, J3.pin2, J4.pin2

notes:
  GND
  IN
  OUT
  VCC
  fet-v2
  +
  -
  Out
  In
