# Fritzing sketch Infrarot-Receiver (saved by Fritzing 0.9.0b)
circuit board: 2cm x 2cm
breadboards: 1

parts:
  Q2 = LTR-301 [package=ltr-301]
  R1 = Resistor [tolerance=±5% resistance=47k package=THT]
  Q3 = NPN-Transistor [package="TO92 [THT]"]
  R2 = Resistor [tolerance=±5% resistance=100k package=THT]
  part = Resistor [tolerance=±5% resistance=220 package=THT]  # not connected
  J1 = male pin header, 3 pins [form="♂ (male)"]
  R3 = Resistor [tolerance=±5% resistance=10k package=THT]

nets:
  N1: Q2.C, R1.Pin_0, R2.Pin_0
  N2: Q2.E, Q3.E, J1.pin3
  N3: R1.Pin_1, J1.pin2, R3.Pin_1
  N4: Q3.B, R2.Pin_1
  N5: Q3.C, J1.pin1, R3.Pin_0

notes:
  IN
  VCC
  GND
  irr-v1
