# Fritzing sketch Infrarot-Sender (saved by Fritzing 0.9.0b)
circuit board: 2cm x 2cm
perfboards: 1

parts:
  LED1 = LED - 3mm [color="Infrared (850nm)" package="3 mm [THT]"]
  R1 = Resistor [tolerance=±5% resistance=47 package=THT]
  R2 = Resistor [tolerance=±5% resistance=1k package=THT]
  J1 = male pin header, 3 pins [form="♂ (male)"]
  Q1 = NPN-Transistor [package="TO92 [THT]"]

nets:
  N1: LED1.cathode, Q1.C
  N2: LED1.anode, R1.Pin_0
  N3: R1.Pin_1, J1.pin2
  N4: R2.Pin_0, Q1.B
  N5: R2.Pin_1, J1.pin1
  N6: J1.pin3, Q1.E

notes:
  irs-v1
  GND
  VCC
  S
