# Fritzing sketch Lichtschranke (saved by Fritzing 0.8.3b)
circuit board: 4cm x 2cm
breadboards: 1

parts:
  R1 = Resistor [tolerance=±5% resistance=100 package=THT]
  Q1 = NPN-Transistor [package="TO92 [THT]"]
  R2 = Resistor [tolerance=±5% resistance=1k package=THT]
  Q2 = LTR-301 [package=ltr-301]
  J1 = female pin header, 5 pins [form="♀ (female)"]
  R3 = Resistor [tolerance=±5% resistance=10k package=THT]
  R4 = Resistor [tolerance=±5% resistance=1k package=THT]
  Q3 = NPN-Transistor [package="TO92 [THT]"]
  R5 = Resistor [tolerance=±5% resistance=10k package=THT]
  LED1 = LED - 3mm [color="Infrared (850nm)" package="3 mm [THT]"]

nets:
  N1: R1.Pin_0, Q1.C
  N2: R1.Pin_1, LED1.cathode
  N3: Q1.E, J1.pin5, Q3.E, R5.Pin_1
  N4: Q1.B, R2.Pin_0
  N5: R2.Pin_1, J1.pin3
  N6: Q2.C, R3.Pin_0
  N7: Q2.E, R4.Pin_1
  N8: J1.pin2, Q3.C
  N9: J1.pin4, R3.Pin_1, LED1.anode
  N10: R4.Pin_0, Q3.B, R5.Pin_0

notes:
  lb-v1
  GND
  VCC
  OUT
  IN
