# Fritzing sketch ir-receiver (saved by Fritzing 0.9.0b)
circuit board: 2cm x 2cm
perfboards: 1

parts:
  IR1 = TSOP312.., 314.. [package=THT]
  C1 = Electrolytic Capacitor [capacitance=1µF package="100 mil [THT, electrolytic]"]
  J1 = male pin header, 3 pins [form="♂ (male)"]

nets:
  N1: IR1.GND, C1.-, J1.pin3
  N2: IR1.Vs, C1.+, J1.pin2
  N3: IR1.Data, J1.pin1

notes:
  irrcv-v1
  -
  +
  S
