# Fritzing sketch Motor-Modul-Lochraster (saved by Fritzing 0.9.0b)
perfboards: 1

parts:
  IC1 = IC, DIP package, 14 pins [chip_label=DRV8835]  # not connected
  MB = Screw terminal - 2 pins [package=THT]
  VM = Screw terminal - 2 pins [package=THT]
  J2 = male pin header, 4 pins [form="♂ (male)"]  # not connected
  J3 = male pin header, 2 pins [form="♂ (male)"]
  M1 = DC Motor
  JACK1 = 2.1mm Barrel Jack with Terminal Block
  J1 = male pin header, 5 pins [form="♂ (male)"]
  Bauteil1 = Arduino Uno (Rev3)

nets:
  N1: MB.pin1, M1.pin_1
  N2: MB.pin2, M1.pin_2
  N3: VM.pin1, JACK1.POS
  N4: VM.pin2, JACK1.NEG
  N5: J3.pin1, J3.pin2
  N6: J1.pin1, Bauteil1.A2
  N7: J1.pin3, Bauteil1.D3_PWM
  N8: J1.pin4, Bauteil1.5V
  N9: J1.pin5, Bauteil1.GND

notes:
  -
  +
  EA
  PA
  PB
  EB
  motor-v1
