# Fritzing sketch Motor-Modul-v2 (saved by Fritzing 0.9.0b)
circuit board: 3.33752cm x 3.10711cm
perfboards: 1

parts:
  MB = Screw terminal - 2 pins [package=THT]
  VM = Screw terminal - 2 pins [package=THT]
  J2 = male pin header, 4 pins [form="♂ (male)"]
  J1 = male pin header, 5 pins [form="♂ (male)"]
  IC1 = IC, DIP package, 14 pins [chip_label=DRV8835]
  J3 = male pin header, 2 pins [form="♂ (male)"]

nets:
  N1: MB.pin1, IC1.pin4, IC1.pin6
  N2: MB.pin2, IC1.pin3, IC1.pin5
  N3: VM.pin1, IC1.pin2
  N4: VM.pin2, J2.pin2, J2.pin3, J1.pin1, IC1.pin1, IC1.pin14
  N5: J2.pin1, J2.pin4, J1.pin5
  N6: J1.pin2, IC1.pin13, J3.pin1
  N7: J1.pin3, IC1.pin10, IC1.pin12
  N8: J1.pin4, IC1.pin9, IC1.pin11
  N9: IC1.pin8, J3.pin2

notes:
  -
  +
  PB
  EB
  motor-v2
