# Fritzing sketch Stepper-Modul-v2 (saved by Fritzing 0.9.0b)
circuit board: 4cm x 4cm
breadboards: 1

parts:
  C1 = Electrolytic Capacitor [capacitance=1µF package="100 mil [THT, electrolytic]"]
  J3 = male pin header, 2 pins [form="♂ (male)"]
  J4 = male pin header, 2 pins [form="♂ (male)"]
  J5 = male pin header, 2 pins [form="♂ (male)"]
  U1 = mystery part, 16 pins [chip_label=A4988]
  M0 = male pin header, 2 pins [form="♂ (male)"]
  M1 = male pin header, 2 pins [form="♂ (male)"]
  M2 = male pin header, 2 pins [form="♂ (male)"]
  J6 = screw terminal, 4 pins
  J2 = Screw terminal - 2 pins [package=THT]
  J1 = female pin header, 5 pins [form="♀ (female)"]
  J7 = male pin header, 2 pins [form="♂ (male)"]
  J8 = male pin header, 2 pins [form="♂ (male)"]

nets:
  N1: C1.-, U1.pin9, U1.pin15, J2.pin2, J1.pin5, J7.pin2, J8.pin2
  N2: C1.+, U1.pin16, J2.pin1
  N3: J3.pin1, U1.pin10
  N4: J3.pin2, J4.pin1, J5.pin1, M0.pin1, M1.pin1, M2.pin1, J1.pin4
  N5: J4.pin2, U1.pin5
  N6: J5.pin2, U1.pin6
  N7: U1.pin2, M0.pin2
  N8: U1.pin3, M1.pin2
  N9: U1.pin4, M2.pin2
  N10: U1.pin7, J1.pin2
  N11: U1.pin8, J1.pin3
  N12: U1.pin11, J6.pin4
  N13: U1.pin12, J6.pin3
  N14: U1.pin13, J6.pin2
  N15: U1.pin14, J6.pin1
  N16: J1.pin1, J7.pin1, J8.pin1

notes:
  VCC
  GND
  DIR
  STP
  VMOT
  stepper-v2
  2B
  2A
  1A
  1B
  SWI
